# Fritzing sketch CatDoor2 (saved by Fritzing 0.9.3b)
breadboards: 2
stripboards: 1

parts:
  MCU1 = Wemos Lolin32lite
  S1 = Pushbutton [package="[SMD]"]
  R1 = Resistor [tolerance=±5% resistance=10k package="2512 [SMD]"]
  R2 = Resistor [tolerance=±5% resistance=10k package="2512 [SMD]"]
  S2 = Pushbutton [package="[SMD]"]
  LED1 = LEDs [package=led10mm]  # not connected
  Part1 = Adafruit VL53L0X Time of Flight Distance Sensor [part_number="Adafruit #3317"]
  Part2 = Adafruit VL53L0X Time of Flight Distance Sensor [part_number="Adafruit #3317"]
  JP1 = Header 4 [package=screwterminal-3.5mm-4_lock]  # not connected

nets:
  N1: MCU1.pin_1, MCU1.pin_2, MCU1.pin_3, MCU1.pin_4, MCU1.pin_5, MCU1.pin_6, MCU1.pin_7, MCU1.pin_8, MCU1.pin_9, MCU1.pin_10, MCU1.pin_11, MCU1.pin_12, MCU1.pin_13, MCU1.pin_14, MCU1.pin_15, MCU1.pin_16, MCU1.pin_18, MCU1.pin_21, MCU1.pin_34
  N2: S1.Pin_3, S1.Pin_4, R1.Pin_0
  N3: R1.Pin_1, R2.Pin_1, S2.Pin_1, S2.Pin_2, Part1.GND
  N4: R2.Pin_0, S2.Pin_3, S2.Pin_4
  N5: Part1.SDA, Part2.SDA

custom parts:
  Wemos Lolin32lite: Wemos Lolin32 pro wifi and blue tooth board based on the ESP-32 cpu, digital I/Os 22, analog inputs 6, analog outputs 2, clock 240mhz, Flash 4Mbytes, PSRAM 4MB, microSD card slot, lipo battery charger (500ma connection broken out on breadboard but not pcb), usb.
  Adafruit VL53L0X Time of Flight Distance Sensor: The VL53L0X is a Time of Flight distance sensor like no other you've used! The sensor contains a very tiny invisible laser source, and a matching sensor. The VL53L0X can detect the "time of flight", or how long the light has taken to bounce back to the sensor. Since it uses a very narrow light source, it is good for determining distance of only the surface directly in front of it. Unlike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
